# Fritzing sketch IOL_Sensor (saved by Fritzing 0.9.3b)
breadboards: 1

parts:
  Part1 = Arduino Uno (Rev3)
  Q1 = LTR-301 [package=ltr-301]
  R1 = Resistor [tolerance=±5% resistance=10k package=THT]
  Q2 = npn-Powertransistor [package="TO220 [THT]"]
  D1 = Rectifier Diode [part_number=1N4001 package="Melf DO-213 AB [SMD]"]
  R2 = Resistor [tolerance=±5% resistance=1k package="2010 [SMD]"]
  M1 = DC Motor
  VCC1 = Battery block 9V
  C1 = Capacitor [package=cap-pth-small2]

nets:
  N1: Part1.A0, Q1.C, R1.Pin_0
  N2: Part1.D7, R2.Pin_0
  N3: Part1.5V, Q1.E
  N4: Part1.GND, Q2.emitter, D1.anode, VCC1.-
  N5: Q2.base, R2.Pin_1
  N6: Q2.collector, D1.cathode, M1.pin_1, C1.2
  N7: VCC1.+, C1.1
